# Fritzing sketch 7segment (saved by Fritzing 0.9.2b)
breadboards: 1

parts:
  Q1 = NPN-Transistor [package="TO92 [THT]"]
  R1 = Resistor [tolerance=±5% resistance=220 package=THT]
  R2 = Resistor [tolerance=±5% resistance=220 package=THT]
  7_Segment1 = 7 Segment Display
  Part1 = Explore Starter 8051

nets:
  N1: Q1.E, R1.Pin_0
  N2: Q1.B, R2.Pin_1
  N3: Q1.C, 7_Segment1.common_anode
  N4: R1.Pin_1, Part1.+5V
  N5: R2.Pin_0, Part1.P3.0
  N6: 7_Segment1.Segment_E, Part1.P1.4
  N7: 7_Segment1.Segment_D, Part1.P1.3
  N8: 7_Segment1.Segment_C, Part1.P1.2
  N9: 7_Segment1.Segment_DP, Part1.P1.7
  N10: 7_Segment1.Segment_B, Part1.P1.1
  N11: 7_Segment1.Segment_A, Part1.P1.0
  N12: 7_Segment1.Segment_F, Part1.P1.5
  N13: 7_Segment1.Segment_G, Part1.P1.6
